# Fritzing sketch schema (saved by Fritzing 0.9.3b)
breadboards: 1

parts:
  U1 = ESP32S-HiLetgo [part_number=ESP32S-HiLetgo]
  DFPlayer_Mini1 = DFPlayer MINI [package="DIP (Dual Inline) [THT]"]
  SPKR1 = Loudspeaker
  R1 = Resistor [tolerance=±5% resistance=220 package=THT]
  R2 = Resistor [tolerance=±5% resistance=220 package=THT]
  R3 = Resistor [tolerance=±5% resistance=220 package=THT]
  R4 = Resistor [tolerance=±5% resistance=220 package=THT]
  R5 = Resistor [tolerance=±5% resistance=220 package=THT]
  S1 = Momentary Switch [package=ksa_sealed_tac_switch]
  S2 = Momentary Switch [package=ksa_sealed_tac_switch]
  S3 = Momentary Switch [package=ksa_sealed_tac_switch]
  S4 = Momentary Switch [package=ksa_sealed_tac_switch]

nets:
  N1: U1.GPIO25, S4.1
  N2: U1.GPIO26, S3.1
  N3: U1.GPIO27, S2.1
  N4: U1.GND, S1.1
  N5: U1.GPIO11, R2.Pin_1, R3.Pin_1, R4.Pin_1, R5.Pin_1
  VIN: U1.VIN, DFPlayer_Mini1.VCC
  N6: U1.GPIO6, S1.4, S2.4, S3.4, S4.4
  N7: U1.GPIO7, DFPlayer_Mini1.GND#6
  N8: U1.GPIO0, DFPlayer_Mini1.TX
  N9: U1.GPIO4, R1.Pin_1
  N10: DFPlayer_Mini1.RX, R1.Pin_0
  N11: DFPlayer_Mini1.SPK1, SPKR1.pin2
  N12: DFPlayer_Mini1.SPK2, SPKR1.pin1
  N13: R2.Pin_0, S2.2
  N14: R3.Pin_0, S1.2
  N15: R4.Pin_0, S4.2
  N16: R5.Pin_0, S3.2

notes:
  1K
  10K
  Vin
  Vcc

custom parts:
  ESP32S-HiLetgo: HiLetgo ESP-WROOM-32 ESP32 ESP-32S Development Board 2.4GHz Dual-Mode WiFi + Bluetooth Dual Cores Microcontroller The ESP32 integrated with Antenna switches, RF Balun, power amplifiers, low-noise amplifiers, filters, and management modules, and the entire solution occupies the least area of PCB. 2.4 GHz Wi-Fi plus Bluetooth dual-mode chip, with TSMC Ultra-low power consumption 40nm technology,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
  DFPlayer MINI: MP3 module by DFRobot.com for playing Music from an SD-Card. Supports WAV and MP3 files.
